// Logisim project Lab6_ALU.circ as structural Verilog: 9 circuits, main circuit main
module main (
  input  [3:0] A,
  input  [3:0] B,
  input  [1:0] S,
  output [3:0] ALU_OUT
);
endmodule

module MUX2to1_1bit (
  input  A,
  input  B,
  input  S,
  output F
);
endmodule

module MUX2to1_4bit (
  input  [3:0] A,
  input  [3:0] B,
  input  S,
  output [3:0] F
);
endmodule

module Full_Adder (
  input  A,
  input  B,
  input  Cin,
  output S,
  output Cout
);
endmodule

module AND_4bit (
  input  [3:0] A,
  input  [3:0] B,
  output [3:0] AND4
);
endmodule

module OR_4bit (
  input  [3:0] A,
  input  [3:0] B,
  output [3:0] OR4
);
endmodule

module XOR_4bit (
  input  [3:0] A,
  input  [3:0] B,
  output [3:0] XOR4
);
endmodule

module MUX4to1_4bit (
  input  [3:0] IN0,
  input  [3:0] IN2,
  input  [3:0] IN1,
  input  [3:0] IN3,
  input  [1:0] S,
  output [3:0] MUX_out
);


  // Notes on the sheet:
  //   (A input)
  //   (C input)
  //   (B input)
  //   (D input)
  //   (F)
endmodule

module Add_4bit (
  input  [3:0] A,
  input  [3:0] B,
  output [3:0] ADD4
);
endmodule
