// Logisim project Ring_Counter.circ as structural Verilog: 1 circuit, main circuit main
module main (
  input  Reset,
  output Q2,
  output Q1,
  output Q0
);

  Clock clk ();  // open: out
  D_Flip_Flop d_ff_1 ();  // open: clk, D, Q, Qn, preset, reset
  D_Flip_Flop d_ff_2 ();  // open: clk, D, Q, Qn, preset, reset
  D_Flip_Flop d_ff_3 ();  // open: clk, D, Q, Qn, preset, reset
endmodule
