// Logisim project Up_Counter.circ as structural Verilog: 2 circuits, main circuit main
module main (
  output Q2,
  output Q1,
  output Q0
);

  Clock clk ();  // open: out
  IFL ifl_1 ();  // open: Q2, Q1, Q0, N2, N1, N0
  D_Flip_Flop d_ff_1 ();  // open: clk, D, Q, Qn, preset, reset
  D_Flip_Flop d_ff_2 ();  // open: clk, D, Q, Qn, preset, reset
  D_Flip_Flop d_ff_3 ();  // open: clk, D, Q, Qn, preset, reset
endmodule

module IFL (
  input  Q2,
  input  Q1,
  input  Q0,
  output N2,
  output N1,
  output N0
);


  // Notes on the sheet:
  //   This input forming logic only contains AND, OR, and NOT gates
endmodule
